# Fritzing sketch DS18B20P (saved by Fritzing 0.8.7b)
breadboards: 1

parts:
  T1 = TMP36 Temperature Sensor [package="TO92 [THT]"]
  Pi1 = Adafruit Pi Cobbler
  R1 = Resistor [tolerance=±5% resistance=1k package=THT]

nets:
  N1: T1.Vout, Pi1.#4, R1.Pin_1
  GND: T1.GND, Pi1.GND
  N2: Pi1.3V3, R1.Pin_0

custom parts:
  Adafruit Pi Cobbler: Adafruit Pi Cobbler GPIO Breakout for Raspberry Pi
